# Fritzing sketch test_barometer (saved by Fritzing 0.9.3b)
breadboards: 1

parts:
  Arduino_nano = Arduino Nano (Rev3.0)
  Barometer = Barometric Pressure Sensor - BMP180 Breakout (GY-68)
  R1 = Resistor [tolerance=±5% resistance=10k package=THT]
  R2 = Resistor [tolerance=±5% resistance=10k package=THT]

nets:
  GND: Arduino_nano.GND, Barometer.GND
  N1: Arduino_nano.A5, R2.Pin_1
  N2: Arduino_nano.A4, R1.Pin_1
  3V3: Arduino_nano.3V3, Barometer.VCC
  N3: Barometer.SCL, R2.Pin_0
  N4: Barometer.SDA, R1.Pin_0
