# Fritzing sketch test_dht22 (saved by Fritzing 0.9.3b)
breadboards: 1

parts:
  Arduino_nano = Arduino Nano (Rev3.0) (ICSP)
  DHT22 = mystery part, 4 pins [chip_label=DHT22]
  R1 = Resistor [tolerance=±5% resistance=10k package=THT]

nets:
  N1: Arduino_nano.D9, DHT22.pin2, R1.Pin_0
  N2: Arduino_nano.GND, DHT22.pin4
  N3: Arduino_nano.5V, DHT22.pin1, R1.Pin_1
