# Fritzing sketch test_ntc_330 (saved by Fritzing 0.9.3b)
breadboards: 1

parts:
  Arduino_nano = Arduino Nano (Rev3.0)
  NTC_Thermistor = mystery part, 2 pins [chip_label=TTC05020JSY]
  R1 = Resistor [tolerance=±5% resistance=330 package=THT]

nets:
  N1: Arduino_nano.5V, NTC_Thermistor.pin1
  N2: Arduino_nano.A1, R1.Pin_1
  N3: NTC_Thermistor.pin2, R1.Pin_0
