# Fritzing sketch Weatherstation (saved by Fritzing 0.9.3b)
breadboards: 1

parts:
  Microprocessor = Arduino Nano (Rev3.0)
  Barometer = Barometric Pressure Sensor - BMP180 Breakout (GY-68)
  R2 = Resistor [tolerance=±5% resistance=10k package=THT]
  R3 = Resistor [tolerance=±5% resistance=10k package=THT]
  IR_Breakbeam_-_receiver_3 = mystery part, 3 pins [chip_label="IR Receiver"]
  IR_Breakbeam_-_receiver_2 = mystery part, 3 pins [chip_label="IR Receiver"]
  IR_Breakbeam_-_receiver_1 = mystery part, 3 pins [chip_label="IR Receiver"]
  IR_Breakbeam_-_led_1 = mystery part, 2 pins [chip_label="IR led"]
  DHT22 = mystery part, 4 pins [chip_label=DHT22]
  R1 = Resistor [tolerance=±5% resistance=10k package=THT]
  IR_Breakbeam_-_led_2 = mystery part, 2 pins [chip_label="IR led"]
  IR_Breakbeam_-_led_3 = mystery part, 2 pins [chip_label="IR led"]
  Hall_effect = mystery part, 3 pins [chip_label=US5881-LUA]
  R4 = Resistor [tolerance=±5% resistance=10k package=THT]

nets:
  GND: Microprocessor.GND, Barometer.GND, IR_Breakbeam_-_receiver_3.pin2, IR_Breakbeam_-_receiver_2.pin2, IR_Breakbeam_-_receiver_1.pin2, IR_Breakbeam_-_led_1.pin2, DHT22.pin4, IR_Breakbeam_-_led_2.pin2, IR_Breakbeam_-_led_3.pin2, Hall_effect.pin2
  N1: Microprocessor.D3, Hall_effect.pin3, R4.Pin_1
  N2: Microprocessor.D5, IR_Breakbeam_-_receiver_1.pin3
  N3: Microprocessor.D6, IR_Breakbeam_-_receiver_2.pin3
  N4: Microprocessor.D7, IR_Breakbeam_-_receiver_3.pin3
  N5: Microprocessor.5V, IR_Breakbeam_-_receiver_3.pin1, IR_Breakbeam_-_receiver_2.pin1, IR_Breakbeam_-_receiver_1.pin1, IR_Breakbeam_-_led_1.pin1, DHT22.pin1, R1.Pin_1, IR_Breakbeam_-_led_2.pin1, IR_Breakbeam_-_led_3.pin1, Hall_effect.pin1, R4.Pin_0
  N6: Microprocessor.A5, R3.Pin_1
  N7: Microprocessor.A4, R2.Pin_1
  3V3: Microprocessor.3V3, Barometer.VCC, Barometer.SCL, Barometer.SDA, R2.Pin_0, R3.Pin_0
  N8: Microprocessor.D13/SCK, DHT22.pin2, R1.Pin_0
