# Fritzing sketch Weerstation (saved by Fritzing 0.9.3b)
breadboards: 1

parts:
  Microprocessor = Arduino Nano (Rev3.0)
  Hall_Effect_sensor = mystery part, 3 pins [chip_label=US5881-LUA]
  DHT1 = DHT22 Humidity and Temperature Sensor
  R1 = Resistor [tolerance=±5% resistance=10k package=THT]
  R2 = Resistor [tolerance=±5% resistance=10k package=THT]

nets:
  GND: Microprocessor.GND, Hall_Effect_sensor.pin2, DHT1.GND
  N1: Microprocessor.D3, Hall_Effect_sensor.pin3, R1.Pin_1
  5V: Microprocessor.5V, Hall_Effect_sensor.pin1, DHT1.VDD, R1.Pin_0, R2.Pin_0
  N2: Microprocessor.D13/SCK, DHT1.DATA, R2.Pin_1
