# Fritzing sketch result_ir_breakbeam (saved by Fritzing 0.9.3b)
breadboards: 1

parts:
  Arduino_nano = Arduino Nano (Rev3.0)
  IR_Breakbeam_-_receiver_3 = mystery part, 3 pins [chip_label="IR Receiver"]
  IR_Breakbeam_-_led_1 = mystery part, 2 pins [chip_label="IR led"]
  IR_Breakbeam_-_receiver_2 = mystery part, 3 pins [chip_label="IR Receiver"]
  IR_Breakbeam_-_led_2 = mystery part, 2 pins [chip_label="IR led"]
  IR_Breakbeam_-_receiver_1 = mystery part, 3 pins [chip_label="IR Receiver"]
  IR_Breakbeam_-_led_3 = mystery part, 2 pins [chip_label="IR led"]

nets:
  N1: Arduino_nano.GND, IR_Breakbeam_-_receiver_3.pin2, IR_Breakbeam_-_led_1.pin2, IR_Breakbeam_-_receiver_2.pin2, IR_Breakbeam_-_led_2.pin2, IR_Breakbeam_-_receiver_1.pin2, IR_Breakbeam_-_led_3.pin2
  N2: Arduino_nano.D5, IR_Breakbeam_-_receiver_1.pin3
  N3: Arduino_nano.D6, IR_Breakbeam_-_receiver_2.pin3
  N4: Arduino_nano.D7, IR_Breakbeam_-_receiver_3.pin3
  N5: Arduino_nano.5V, IR_Breakbeam_-_receiver_3.pin1, IR_Breakbeam_-_led_1.pin1, IR_Breakbeam_-_receiver_2.pin1, IR_Breakbeam_-_led_2.pin1, IR_Breakbeam_-_receiver_1.pin1, IR_Breakbeam_-_led_3.pin1
