# Fritzing sketch test_grove_encoder (saved by Fritzing 0.9.3b)
breadboards: 1

parts:
  Arduino_nano = Arduino Nano (Rev3.0) (ICSP)
  Encoder = mystery part, 4 pins [chip_label="Grove Encoder"]

nets:
  N1: Arduino_nano.GND, Encoder.pin4
  N2: Arduino_nano.D2, Encoder.pin2
  N3: Arduino_nano.D3, Encoder.pin1
  N4: Arduino_nano.5V, Encoder.pin3
