# Fritzing sketch test_ir_breakbeam_dig&ana (saved by Fritzing 0.9.3b)
breadboards: 1

parts:
  Arduino_nano_-_Analoog = Arduino Nano (Rev3.0)
  Arduino_nano_-_Digitaal = Arduino Nano (Rev3.0)
  IR_Breakbeam_-_receiver = mystery part, 3 pins [chip_label="IR Receiver"]
  IR_Breakbeam_-_led = mystery part, 2 pins [chip_label="IR led"]
  IR_Breakbeam_-_receiver_2 = mystery part, 3 pins [chip_label="IR Receiver"]
  IR_Breakbeam_-_led_2 = mystery part, 2 pins [chip_label="IR led"]

nets:
  N1: Arduino_nano_-_Analoog.GND, IR_Breakbeam_-_receiver_2.pin2, IR_Breakbeam_-_led_2.pin2
  N2: Arduino_nano_-_Analoog.5V, IR_Breakbeam_-_receiver_2.pin1, IR_Breakbeam_-_led_2.pin1
  N3: Arduino_nano_-_Analoog.A3, IR_Breakbeam_-_receiver_2.pin3
  N4: Arduino_nano_-_Digitaal.GND, IR_Breakbeam_-_receiver.pin2, IR_Breakbeam_-_led.pin2
  N5: Arduino_nano_-_Digitaal.D9, IR_Breakbeam_-_receiver.pin3
  N6: Arduino_nano_-_Digitaal.5V, IR_Breakbeam_-_receiver.pin1, IR_Breakbeam_-_led.pin1
