# Fritzing sketch test_ir_led_and_receiver (saved by Fritzing 0.9.3b)
breadboards: 1

parts:
  Arduino_nano = Arduino Nano (Rev3.0)
  IR_Receiver = mystery part, 3 pins [chip_label="ROHM Semiconductor RPM7138-H4R"]
  IR_LED = mystery part, 2 pins [chip_label="Harvatek HE1-120AC IR-emitter"]

nets:
  N1: Arduino_nano.GND, IR_Receiver.pin2, IR_LED.pin2
  N2: Arduino_nano.D9, IR_Receiver.pin1
  N3: Arduino_nano.5V, IR_Receiver.pin3, IR_LED.pin1
