# Fritzing sketch test_lineair (saved by Fritzing 0.9.3b)
breadboards: 1

parts:
  Arduino_nano = Arduino Nano (Rev3.0)
  Hall_effect_lineair = mystery part, 3 pins [chip_label=AH3503UA]
  R1 = Resistor [tolerance=±5% resistance=10k package=THT]

nets:
  N1: Arduino_nano.D4, Hall_effect_lineair.pin3, R1.Pin_1
  N2: Arduino_nano.GND, Hall_effect_lineair.pin2
  N3: Arduino_nano.5V, Hall_effect_lineair.pin1, R1.Pin_0
