# Fritzing sketch test_unipolar (saved by Fritzing 0.9.3b)
breadboards: 1

parts:
  Arduino_nano = Arduino Nano (Rev3.0)
  Hall_effect_unipolar = mystery part, 3 pins [chip_label=US5881-LUA]
  R1 = Resistor [tolerance=±5% resistance=10k package=THT]

nets:
  N1: Arduino_nano.D4, Hall_effect_unipolar.pin3, R1.Pin_1
  N2: Arduino_nano.GND, Hall_effect_unipolar.pin2
  N3: Arduino_nano.5V, Hall_effect_unipolar.pin1, R1.Pin_0
